# Fritzing sketch projeto_esquema_eletrico (saved by Fritzing 0.9.3b)
breadboards: 2

parts:
  LCM1602_IIC1 = LCM1602 IIC [part_number="LCM1602 IIC" chip_label="LCM1602 IIC" package="DIP (Dual Inline) [THT]"]
  U1 = LCD-16X2 [package=lcd-16x2]
  DI1 = 7 Segment Display
  J1 = Piezo Speaker
  S1 = Pushbutton [package="[THT]"]
  S2 = Pushbutton [package="[THT]"]
  S3 = Pushbutton [package="[THT]"]
  S4 = Pushbutton [package="[THT]"]
  Componente1 = Bluetooth HC-05 Macho
  LED1 = LED - 3mm [color="Blue (470nm)" package="3 mm [THT]"]
  LED2 = LED - 3mm [color="Blue (470nm)" package="3 mm [THT]"]
  LED3 = LED - 3mm [color="Blue (470nm)" package="3 mm [THT]"]
  LED4 = LED - 3mm [color="Blue (470nm)" package="3 mm [THT]"]
  Componente2 = Arduino Uno (Rev3) - ICSP
  R1 = Resistor [tolerance=±5% resistance=220 package="2512 [SMD]"]
  R2 = Resistor [tolerance=±5% resistance=220 package="2512 [SMD]"]
  R3 = Resistor [tolerance=±5% resistance=220 package="2512 [SMD]"]
  R4 = Resistor [tolerance=±5% resistance=220 package="2512 [SMD]"]
  R5 = Resistor [tolerance=±5% resistance=220 package=THT]
  R6 = Resistor [tolerance=±5% resistance=220 package=THT]
  R7 = Resistor [tolerance=±5% resistance=220 package=THT]
  R8 = Resistor [tolerance=±5% resistance=220 package=THT]
  R9 = Resistor [tolerance=±5% resistance=330 package="2512 [SMD]"]
  R10 = Resistor [tolerance=±5% resistance=10 package=THT]
  R11 = Resistor [tolerance=±5% resistance=2.2k package=THT]
  R12 = Resistor [tolerance=±5% resistance=1.5k package=THT]

nets:
  VSS: LCM1602_IIC1.VSS, U1.VSS
  VDD: LCM1602_IIC1.VDD, U1.VDD
  N1: LCM1602_IIC1.V0, U1.VO
  N2: LCM1602_IIC1.RS, U1.RS
  N3: LCM1602_IIC1.RW, U1.R_W
  N4: LCM1602_IIC1.E, U1.E
  N5: LCM1602_IIC1.D0, U1.DB0
  N6: LCM1602_IIC1.D1, U1.DB1
  N7: LCM1602_IIC1.D2, U1.DB2
  N8: LCM1602_IIC1.D3, U1.DB3
  N9: LCM1602_IIC1.D4, U1.DB4
  N10: LCM1602_IIC1.D5, U1.DB5
  N11: LCM1602_IIC1.D6, U1.DB6
  N12: LCM1602_IIC1.D7, U1.DB7
  N13: LCM1602_IIC1.A, U1.A
  N14: LCM1602_IIC1.K, U1.K
  GND: LCM1602_IIC1.GND, J1.pin1, Componente1.GND, LED1.cathode, LED2.cathode, LED3.cathode, LED4.cathode, Componente2.GND, R5.Pin_1, R6.Pin_1, R7.Pin_1, R8.Pin_1, R9.Pin_0, R11.Pin_1
  VCC: LCM1602_IIC1.VCC, S1.Pin_3, S1.Pin_4, S2.Pin_3, S2.Pin_4, S3.Pin_3, S3.Pin_4, S4.Pin_3, S4.Pin_4, Componente1.VCC, Componente2.5V
  N15: LCM1602_IIC1.SDA, Componente2.A5/SCL
  N16: LCM1602_IIC1.SCL, Componente2.A4/SDA
  N17: LCM1602_IIC1.LED_A, LCM1602_IIC1.LED_B
  N18: DI1.Segment_E, Componente2.D10_PWM/SS
  N19: DI1.Segment_D, Componente2.D9_PWM
  N20: DI1.common_anode, R9.Pin_1
  N21: DI1.Segment_C, Componente2.D8
  N22: DI1.Segment_B, Componente2.D7
  N23: DI1.Segment_A, Componente2.D6_PWM
  N24: DI1.Segment_F, Componente2.ICSP_MOSI, Componente2.D11_PWM/MOSI
  N25: DI1.Segment_G, Componente2.ICSP_MISO, Componente2.D12/MISO
  N26: J1.pin2, R10.Pin_1
  N27: S1.Pin_1, S1.Pin_2, Componente2.D2, R8.Pin_0
  N28: S2.Pin_1, S2.Pin_2, Componente2.D3_PWM, R7.Pin_0
  N29: S3.Pin_1, S3.Pin_2, Componente2.D4, R6.Pin_0
  N30: S4.Pin_1, S4.Pin_2, Componente2.D5_PWM, R5.Pin_0
  N31: Componente1.TXD, Componente2.D0/RX
  N32: Componente1.RXD, R11.Pin_0, R12.Pin_1
  N33: LED1.anode, R1.Pin_0
  N34: LED2.anode, R3.Pin_0
  N35: LED3.anode, R2.Pin_0
  N36: LED4.anode, R4.Pin_0
  N37: Componente2.A0, R2.Pin_1
  N38: Componente2.A1, R1.Pin_1
  N39: Componente2.A2, R3.Pin_1
  N40: Componente2.A3, R4.Pin_1
  N41: Componente2.D13/SCK, R10.Pin_0
  N42: Componente2.D1/TX, R12.Pin_0

custom parts:
  LCM1602 IIC: I2C-Module to use a 1602 or 2004 LCD on with the wire.h libory Serial LCD Modul

// code stored in the sketch: ProjetoMicrocontroladores.ino
/* @author: Lucas Lacerda (lucaaslb)
 *          Lucas Alves 
 *          Thauan Trindade
    Projeto Automação residêncial
    MICROCONTROLADORES - UAM - CCO 6° SEMESTRE
    Setembro / 2018
*/


#include <LiquidCrystal_I2C.h>

// Componetes e pinos Arduino
#define LED00 A0
#define LED01 A1
#define LED02 A2
#define LED03 A3
#define BTNLED00 2
#define BTNLED01 3
#define BTNLED02 4
#define BTNLED03 5

#define DISPLAY7_A 6
#define DISPLAY7_B 7
#define DISPLAY7_C 8
#define DISPLAY7_D 9
#define DISPLAY7_E 10
#define DISPLAY7_F 11
#define DISPLAY7_G 12

#define BUZZ 13

//Variaveis globais;
LiquidCrystal_I2C lcd(0x3F, 2, 1, 0, 4, 5, 6, 7, 3, POSITIVE);

void setup() {
  pinMode(LED00, OUTPUT);
  pinMode(LED01, OUTPUT);
  pinMode(LED02, OUTPUT);
  pinMode(LED03, OUTPUT);

  pinMode(BTNLED00, INPUT);
  pinMode(BTNLED01, INPUT);
  pinMode(BTNLED02, INPUT);
  pinMode(BTNLED03, INPUT);

  pinMode(BUZZ, OUTPUT);

  pinMode(DISPLAY7_A, OUTPUT); //Pino 6 do Arduino ligado ao segmento A
  pinMode(DISPLAY7_B, OUTPUT); //Pino 7 do Arduino ligado ao segmento B
  pinMode(DISPLAY7_C, OUTPUT); //Pino 8 do Arduino ligado ao segmento C
  pinMode(DISPLAY7_D, OUTPUT); //Pino 9 do Arduino ligado ao segmento D
  pinMode(DISPLAY7_E, OUTPUT); //Pino 10 do Arduino ligado ao segmento E
  pinMode(DISPLAY7_F, OUTPUT); //Pino 11 do Arduino ligado ao segmento F
  pinMode(DISPLAY7_G, OUTPUT); //Pino 12 do Arduino ligado ao segmento G

  Serial.begin(9600);
  lcd.begin (16, 2);
  lcd.noAutoscroll();
  lcd.setBacklight(HIGH);
  lcd.setCursor(0, 0);


  delay(1000);
  writeDisplay("Automacao Resid", 0, 0, true);
  delay(1000);
  writeDisplay("Proj.TRANQUILO!", 0, 1, false);

  delay(1500);

  writeDisplay("SEJA BEM", 4, 0, true);
  writeDisplay("VINDO", 5, 1, false);

  delay(1500);

  msgDefault();
}

void loop() {
  btnLedOnOff();
  readSerial();
}


void beep() {
  tone(BUZZ, 1000);
  delay(200);
  noTone(BUZZ);
}


void tenSeconds(byte digit) {
  byte seven_seg_digits[16][7] = {
    { 1, 1, 1, 1, 1, 1, 0 }, // = Digito 0
    { 0, 1, 1, 0, 0, 0, 0 }, // = Digito 1
    { 1, 1, 0, 1, 1, 0, 1 }, // = Digito 2
    { 1, 1, 1, 1, 0, 0, 1 }, // = Digito 3
    { 0, 1, 1, 0, 0, 1, 1 }, // = Digito 4
    { 1, 0, 1, 1, 0, 1, 1 }, // = Digito 5
    { 1, 0, 1, 1, 1, 1, 1 }, // = Digito 6
    { 1, 1, 1, 0, 0, 0, 0 }, // = Digito 7
    { 1, 1, 1, 1, 1, 1, 1 }, // = Digito 8
    { 1, 1, 1, 0, 0, 1, 1 }, // = Digito 9
    { 0, 0, 0, 0, 0, 0, 0 }
  };
  byte pin = 6;

  //Percorre o array ligando os segmentos correspondentes ao digito
  for (byte segCount = 0; segCount < 7; ++segCount) {
    digitalWrite(pin, seven_seg_digits[digit][segCount]);
    pin++;
  }
  delay(50);
}


void btnLedOnOff() {

  if (digitalRead(BTNLED00)) {
    digitalWrite(LED00, !digitalRead(LED00));
    delay(500);
  }

  if (digitalRead(BTNLED01)) {
    digitalWrite(LED01, !digitalRead(LED01));
    delay(500);
  }

  if (digitalRead(BTNLED02)) {
    digitalWrite(LED02, !digitalRead(LED02));
    delay(500);
  }

  if (digitalRead(BTNLED03)) {
    digitalWrite(LED03, !digitalRead(LED03));
    delay(500);
  }

}

void readSerial() {
  byte contador;
  switch (Serial.read()) {
    case '0':
      turnLedOff();
      Serial.println("Efeito 1 - FLASHES ALL");
      writeDisplay("Efeito 1", 0, 0, true);
      writeDisplay("FLASHES ALL", 3, 1, false);

      for (contador = 0; contador < 10; contador++) {
        tenSeconds(contador);
        effect00();
      }
      tenSeconds(contador);
      beep();
      msgDefault();
      break;

    case '1':
      turnLedOff();
      Serial.println("Efeito 2 - Boomerang");
      writeDisplay("Efeito 2", 0, 0, true);
      writeDisplay("Boomerang", 2, 1, false);

      for (contador = 0; contador < 10; contador++) {
        tenSeconds(contador);

        digitalWrite(LED00, HIGH);
        delay(135);
        digitalWrite(LED00, LOW);
        digitalWrite(LED01, HIGH);
        delay(135);
        digitalWrite(LED01, LOW);
        digitalWrite(LED02, HIGH);
        delay(135);
        digitalWrite(LED02, LOW);
        digitalWrite(LED03, HIGH);
        delay(135);
        digitalWrite(LED03, LOW);
        digitalWrite(LED02, HIGH);
        delay(135);
        digitalWrite(LED02, LOW);
        digitalWrite(LED01, HIGH);
        delay(135);
        digitalWrite(LED01, LOW);
        delay(135);
      }

      tenSeconds(contador);
      turnLedOff();
      beep();
      msgDefault();
      break;

    case '2':
      turnLedOff();
      Serial.println("Efeito 3 - Pares");
      writeDisplay("Efeito 3", 0, 0, true);
      writeDisplay("Pares", 2, 1, false);

      for (contador = 0; contador < 10; contador++) {
        tenSeconds(contador);
        digitalWrite(LED00, HIGH);
        digitalWrite(LED01, HIGH);
        delay(270);
        digitalWrite(LED00, LOW);
        digitalWrite(LED01, LOW);

        delay(200);
        digitalWrite(LED02, HIGH);
        digitalWrite(LED03, HIGH);
        delay(270);
        digitalWrite(LED02, LOW);
        digitalWrite(LED03, LOW);

        delay(200);
      }
      tenSeconds(contador);
      turnLedOff();
      beep();
      msgDefault();
      break;

    case '3':
      turnLedOff();
      Serial.println("Efeito 4 - RANDOM");
      writeDisplay("Efeito 3", 0, 0, true);
      writeDisplay("RANDOM", 2, 1, false);

      for (contador = 0; contador < 10; contador++) {
        tenSeconds(contador);
        effect03();
      }
      tenSeconds(contador);
      turnLedOff();
      beep();
      msgDefault();
      break;

  }

}

void writeDisplay(String msg, int column, int line, bool clearDisplay) {

  if (clearDisplay) lcd.clear();

  lcd.setCursor(column, line);
  lcd.print(msg);
}

void turnLedON() {
  digitalWrite(LED00, HIGH);
  digitalWrite(LED01, HIGH);
  digitalWrite(LED02, HIGH);
  digitalWrite(LED03, HIGH);
}

void turnLedOff() {
  digitalWrite(LED00, LOW);
  digitalWrite(LED01, LOW);
  digitalWrite(LED02, LOW);
  digitalWrite(LED03, LOW);
}

void msgDefault() {
  writeDisplay("APS", 7, 0, true);
  writeDisplay("MICROCONTROLADORES", 0, 1, false);
}

void effect00() {
  for (int i = 0; i < 10; i++) {
    turnLedON();
    delay(50);
    turnLedOff();
    delay(50);
  }
}

void effect03() {
  int LEDS[] = {A0, A1, A2, A3};
  for (int i = 0; i < 4; i++) {
    int STATUS = random(0, 2); // entre 0 e 1
    digitalWrite(LEDS[i], STATUS);
    delay(200);
  }
  turnLedOff();
}
